// Logisim project Aula 2.circ as structural Verilog: 7 circuits, main circuit main
module main (
  input  in_1,
  input  in_2,
  input  in_3,
  input  [3:0] in_4,
  input  [3:0] in_5,
  input  [3:0] in_6
);

  wire [15:0] sla_1_sa, sla_1_sb, ula_1_out_4;

  sla sla_1 (
    .Clock(in_1), .Enable(in_2), .Reset(in_3), .AdressA(in_4), .AdressB(in_5), .Data(ula_1_out_4),
    .SB(sla_1_sb), .SA(sla_1_sa));
  // Probe on sla_1_sb
  // Probe on sla_1_sb
  // Probe on sla_1_sa
  // Probe on sla_1_sa
  ULA ula_1 (.A(sla_1_sb), .B(sla_1_sa), .out_4(ula_1_out_4), .Op(in_6));  // open: out_5, out_6, out_7
  // Probe on in_6
  // Probe on ula_1_out_4
  // Probe on ula_1_out_4
endmodule

// Reset
module Aula_2 (
  input  Set,
  input  Reset,
  input  Data,
  input  Enable,
  output S,
  output out_6,
  output S_2
);

  wire and_1_out, and_2_out, and_3_out, and_4_out, and_5_out, and_6_out, not_3_out, not_4_out, not_5_out,
       not_7_out;

  not not_1 (S, and_1_out);
  and and_1 (and_1_out, Set, out_6);
  and and_2 (and_2_out, S, Reset);
  not not_2 (out_6, and_2_out);
  not not_3 (not_3_out, Data);
  and and_3 (and_3_out, Data, Enable);
  and and_4 (and_4_out, Enable, not_3_out);
  not not_4 (not_4_out, and_3_out);
  and and_5 (and_5_out, not_4_out, not_7_out);
  and and_6 (and_6_out, S_2, not_5_out);
  not not_5 (not_5_out, and_4_out);
  not not_6 (S_2, and_5_out);
  not not_7 (not_7_out, and_6_out);
endmodule

module sla (
  input  Clock,
  input  Enable,
  input  Reset,
  input  [3:0] AdressA,
  input  [3:0] AdressB,
  input  [15:0] Data,
  output [15:0] SB,
  output [15:0] SA
);

  wire en0, en1, en2, en3, en4, en5, en6, en7, en8, en9, en10, en11, en12, en13, en14, en15;
  wire [15:0] out0, out1, out2, out3, out4, out5, out6, out7, out8, out9, out10, out11, out12, out13, out14,
       out15;

  Demultiplexer #(.select(4)) demultiplexer_1 (
    .out0(en0), .out1(en1), .out2(en2), .out3(en3), .out4(en4), .out5(en5), .out6(en6), .out7(en7),
    .out8(en8), .out9(en9), .out10(en10), .out11(en11), .out12(en12), .out13(en13), .out14(en14),
    .out15(en15), .in(Enable), .sel(AdressA));  // open: en
  Register #(.width(16)) register_1 (.D(Data), .en(en0), .Q(out0), .clk(Clock), .clr(Reset));
  Register #(.width(16)) register_2 (.D(Data), .en(en1), .Q(out1), .clk(Clock), .clr(Reset));
  Register #(.width(16)) register_3 (.D(Data), .en(en2), .Q(out2), .clk(Clock), .clr(Reset));
  Register #(.width(16)) register_4 (.D(Data), .en(en3), .Q(out3), .clk(Clock), .clr(Reset));
  Register #(.width(16)) register_5 (.D(Data), .en(en4), .Q(out4), .clk(Clock), .clr(Reset));
  Register #(.width(16)) register_6 (.D(Data), .en(en5), .Q(out5), .clk(Clock), .clr(Reset));
  Register #(.width(16)) register_7 (.D(Data), .en(en6), .Q(out6), .clk(Clock), .clr(Reset));
  Register #(.width(16)) register_8 (.D(Data), .en(en7), .Q(out7), .clk(Clock), .clr(Reset));
  Register #(.width(16)) register_9 (.D(Data), .en(en8), .Q(out8), .clk(Clock), .clr(Reset));
  Register #(.width(16)) register_10 (.D(Data), .en(en9), .Q(out9), .clk(Clock), .clr(Reset));
  Register #(.width(16)) register_11 (.D(Data), .en(en10), .Q(out10), .clk(Clock), .clr(Reset));
  Register #(.width(16)) register_12 (.D(Data), .en(en11), .Q(out11), .clk(Clock), .clr(Reset));
  Multiplexer #(.select(4), .width(16)) multiplexer_1 (
    .in0(out0), .in1(out1), .in2(out2), .in3(out3), .in4(out4), .in5(out5), .in6(out6), .in7(out7),
    .in8(out8), .in9(out9), .in10(out10), .in11(out11), .in12(out12), .in13(out13), .in14(out14),
    .in15(out15), .out(SA), .sel(AdressA));  // open: en
  Register #(.width(16)) register_13 (.D(Data), .en(en12), .Q(out12), .clk(Clock), .clr(Reset));
  Register #(.width(16)) register_14 (.D(Data), .en(en13), .Q(out13), .clk(Clock), .clr(Reset));
  Register #(.width(16)) register_15 (.D(Data), .en(en14), .Q(out14), .clk(Clock), .clr(Reset));
  Register #(.width(16)) register_16 (.D(Data), .en(en15), .Q(out15), .clk(Clock), .clr(Reset));
  Multiplexer #(.select(4), .width(16)) multiplexer_2 (
    .in0(out0), .in1(out1), .in2(out2), .in3(out3), .in4(out4), .in5(out5), .in6(out6), .in7(out7),
    .in8(out8), .in9(out9), .in10(out10), .in11(out11), .in12(out12), .in13(out13), .in14(out14),
    .in15(out15), .out(SB), .sel(AdressB));  // open: en

  // Other names for the same wires on the sheet: addA[3:0] = AdressA; addB[3:0] = AdressB; clk = Clock; en = Enable;
  //   rst = Reset
endmodule

module ULA (
  input  [15:0] A,
  input  [15:0] B,
  input  [3:0] Op,
  output [15:0] out_4,
  output out_5,
  output out_6,
  output [4:0] out_7
);

  wire [15:0] OutAnd, OutDiv, OutLeftShift, OutMult, OutNAnd, OutNor, OutNotA, OutNotB, OutOr, OutRightShift,
       OutSub, OutSum, OutXNor, OutXor;

  Adder #(.width(16)) adder_1 (.a(A), .b(B), .out(OutSum));  // open: cin, cout
  Subtractor #(.width(16)) subtractor_1 (.a(A), .b(B), .out(OutSub));  // open: bin, bout
  Multiplier #(.width(16)) multiplier_1 (.a(A), .b(B), .out(OutMult));  // open: cin, cout
  Divider #(.width(16)) divider_1 (.a(A), .b(B), .out(OutDiv));  // open: upper, rem
  Shifter #(.width(16)) shifter_1 (.in(A), .\dist (B[3:0]), .out(OutLeftShift));
  Shifter #(.width(16), .shift("lr")) shifter_2 (.in(A), .\dist (B[3:0]), .out(OutRightShift));
  assign OutNotA = ~A;  // NOT_Gate not_1, 16 bits wide
  assign OutNotB = ~B;  // NOT_Gate not_2, 16 bits wide
  assign OutAnd = A & B;  // AND_Gate and_1, 16 bits wide
  assign OutOr = A | B;  // OR_Gate or_1, 16 bits wide
  assign OutNor = ~(A | B);  // NOR_Gate nor_1, 16 bits wide
  assign OutNAnd = ~(A & B);  // NAND_Gate nand_1, 16 bits wide
  // XOR_Gate xor_1 has open pins: in0=A, in1=B, out=open
  assign OutXNor = ~(A ^ B);  // XNOR_Gate xnor_1, 16 bits wide
  Comparator #(.width(16)) comparator_1 (.a(A), .b(B), .gt(out_5));  // open: eq, lt
  Comparator #(.width(16)) comparator_2 (.a(A), .b(B), .lt(out_6));  // open: gt, eq
  BitAdder #(.width(16)) bitadder_1 (.in0(A), .out(out_7));
  Multiplexer #(.select(4), .width(16)) multiplexer_1 (
    .in0(OutNotA), .in1(OutNotB), .in2(OutAnd), .in3(OutOr), .in4(OutNor), .in5(OutNAnd), .in6(OutXor),
    .in7(OutXNor), .in8(OutSum), .in9(OutSub), .in10(OutMult), .in11(OutDiv), .in12(OutRightShift),
    .in13(OutLeftShift), .out(out_4), .sel(Op));  // open: in14, in15, en
  // Probe on out_7
endmodule

module FullSum (
  input  A,
  input  B,
  input  C_In,
  output S,
  output C_Out
);

  wire halfsum_1_c_out, halfsum_1_s, halfsum_2_c_out;

  HalfSum halfsum_1 (.A(A), .B(B), .S(halfsum_1_s), .C_Out(halfsum_1_c_out));
  HalfSum halfsum_2 (.A(halfsum_1_s), .B(C_In), .S(S), .C_Out(halfsum_2_c_out));
  or or_1 (C_Out, halfsum_2_c_out, halfsum_1_c_out);
endmodule

module HalfSum (
  input  A,
  input  B,
  output S,
  output C_Out
);

  xor xor_1 (S, A, B);
  and and_1 (C_Out, A, B);
endmodule

module Sum (
  input  in_1,
  input  [15:0] A,
  input  [15:0] B,
  output out_4,
  output [15:0] out_5
);

  wire fullsum_1_c_out, fullsum_2_c_out, fullsum_3_c_out, fullsum_5_c_out, fullsum_6_c_out, fullsum_7_c_out,
       fullsum_8_c_out, fullsum_9_c_out, fullsum_10_c_out, fullsum_11_c_out, fullsum_12_c_out,
       fullsum_13_c_out, fullsum_14_c_out, fullsum_15_c_out, fullsum_16_c_out;

  // Probe on out_5
  // Probe on A
  // Probe on B
  FullSum fullsum_1 (.A(fullsum_8_c_out), .B(B[12]), .C_In(A[12]), .S(out_5[12]), .C_Out(fullsum_1_c_out));
  FullSum fullsum_2 (.A(fullsum_1_c_out), .B(B[13]), .C_In(A[13]), .S(out_5[13]), .C_Out(fullsum_2_c_out));
  FullSum fullsum_3 (.A(fullsum_2_c_out), .B(B[14]), .C_In(A[14]), .S(out_5[14]), .C_Out(fullsum_3_c_out));
  FullSum fullsum_4 (.A(fullsum_3_c_out), .B(B[15]), .C_In(A[15]), .S(out_5[15]), .C_Out(out_4));
  FullSum fullsum_5 (.A(fullsum_12_c_out), .B(B[8]), .C_In(A[8]), .S(out_5[8]), .C_Out(fullsum_5_c_out));
  FullSum fullsum_6 (.A(fullsum_5_c_out), .B(B[9]), .C_In(A[9]), .S(out_5[9]), .C_Out(fullsum_6_c_out));
  FullSum fullsum_7 (.A(fullsum_6_c_out), .B(B[10]), .C_In(A[10]), .S(out_5[10]), .C_Out(fullsum_7_c_out));
  FullSum fullsum_8 (.A(fullsum_7_c_out), .B(B[11]), .C_In(A[11]), .S(out_5[11]), .C_Out(fullsum_8_c_out));
  // Probe on out_5
  FullSum fullsum_9 (.A(fullsum_16_c_out), .B(B[4]), .C_In(A[4]), .S(out_5[4]), .C_Out(fullsum_9_c_out));
  FullSum fullsum_10 (.A(fullsum_9_c_out), .B(B[5]), .C_In(A[5]), .S(out_5[5]), .C_Out(fullsum_10_c_out));
  FullSum fullsum_11 (.A(fullsum_10_c_out), .B(B[6]), .C_In(A[6]), .S(out_5[6]), .C_Out(fullsum_11_c_out));
  FullSum fullsum_12 (.A(fullsum_11_c_out), .B(B[7]), .C_In(A[7]), .S(out_5[7]), .C_Out(fullsum_12_c_out));
  FullSum fullsum_13 (.A(in_1), .B(B[0]), .C_In(A[0]), .S(out_5[0]), .C_Out(fullsum_13_c_out));
  FullSum fullsum_14 (.A(fullsum_13_c_out), .B(B[1]), .C_In(A[1]), .S(out_5[1]), .C_Out(fullsum_14_c_out));
  FullSum fullsum_15 (.A(fullsum_14_c_out), .B(B[2]), .C_In(A[2]), .S(out_5[2]), .C_Out(fullsum_15_c_out));
  FullSum fullsum_16 (.A(fullsum_15_c_out), .B(B[3]), .C_In(A[3]), .S(out_5[3]), .C_Out(fullsum_16_c_out));

  // Other names for the same wires on the sheet: A1 = A[0]; A2 = A[1]; A3 = A[2]; A4 = A[3]; A5 = A[4]; A6 = A[5];
  //   A7 = A[6]; A8 = A[7]; A9 = A[8]; A10 = A[9]; A11 = A[10]; A12 = A[11]; A13 = A[12]; A14 = A[13]; A15 = A[14];
  //   A16 = A[15]; B1 = B[0]; B2 = B[1]; B3 = B[2]; B4 = B[3]; B5 = B[4]; B6 = B[5]; B7 = B[6]; B8 = B[7]; B9 = B[8];
  //   B10 = B[9]; B11 = B[10]; B12 = B[11]; B13 = B[12]; B14 = B[13]; B15 = B[14]; B16 = B[15]; Soma[15:0] = out_5;
  //   tunnel = out_4
endmodule
